// Logisim project DQ 寄存器——0x8.circ as structural Verilog: 7 circuits, main circuit main
module main (
  input  in_1,
  input  [7:0] in_2,
  output [7:0] out_3
);

  wire nand_1_out, nand_2_out, nand_3_out, nand_4_out, nand_5_out, nand_6_out, nand_7_out, nand_8_out,
       nand_9_out, nand_10_out, nand_11_out, nand_12_out, nand_13_out, nand_14_out, nand_15_out, nand_16_out,
       nand_18_out, nand_20_out, nand_22_out, nand_24_out, nand_26_out, nand_28_out, nand_30_out,
       nand_32_out, not_1_out, not_2_out, not_3_out, not_4_out, not_5_out, not_6_out, not_7_out, not_8_out;

  not not_1 (not_1_out, in_2[0]);
  not not_2 (not_2_out, in_2[1]);
  not not_3 (not_3_out, in_2[2]);
  not not_4 (not_4_out, in_2[3]);
  not not_5 (not_5_out, in_2[4]);
  not not_6 (not_6_out, in_2[5]);
  not not_7 (not_7_out, in_2[6]);
  not not_8 (not_8_out, in_2[7]);
  nand nand_1 (nand_1_out, in_2[0], in_1);
  nand nand_2 (nand_2_out, not_1_out, in_1);
  nand nand_3 (nand_3_out, in_2[1], in_1);
  nand nand_4 (nand_4_out, not_2_out, in_1);
  nand nand_5 (nand_5_out, in_2[2], in_1);
  nand nand_6 (nand_6_out, not_3_out, in_1);
  nand nand_7 (nand_7_out, in_2[3], in_1);
  nand nand_8 (nand_8_out, not_4_out, in_1);
  nand nand_9 (nand_9_out, in_2[4], in_1);
  nand nand_10 (nand_10_out, not_5_out, in_1);
  nand nand_11 (nand_11_out, in_2[5], in_1);
  nand nand_12 (nand_12_out, not_6_out, in_1);
  nand nand_13 (nand_13_out, in_2[6], in_1);
  nand nand_14 (nand_14_out, not_7_out, in_1);
  nand nand_15 (nand_15_out, in_2[7], in_1);
  nand nand_16 (nand_16_out, not_8_out, in_1);
  nand nand_17 (out_3[0], nand_1_out, nand_18_out);
  nand nand_18 (nand_18_out, nand_2_out, out_3[0]);
  nand nand_19 (out_3[1], nand_3_out, nand_20_out);
  nand nand_20 (nand_20_out, nand_4_out, out_3[1]);
  nand nand_21 (out_3[2], nand_5_out, nand_22_out);
  nand nand_22 (nand_22_out, nand_6_out, out_3[2]);
  nand nand_23 (out_3[3], nand_7_out, nand_24_out);
  nand nand_24 (nand_24_out, out_3[3], nand_8_out);
  nand nand_25 (out_3[4], nand_9_out, nand_26_out);
  nand nand_26 (nand_26_out, out_3[4], nand_10_out);
  nand nand_27 (out_3[5], nand_11_out, nand_28_out);
  nand nand_28 (nand_28_out, out_3[5], nand_12_out);
  nand nand_29 (out_3[6], nand_13_out, nand_30_out);
  nand nand_30 (nand_30_out, out_3[6], nand_14_out);
  nand nand_31 (out_3[7], nand_15_out, nand_32_out);
  nand nand_32 (nand_32_out, out_3[7], nand_16_out);
endmodule

module \sq寄存器单元  (
  output [7:0] out_1
);

  wire clock_1_out;

  main main_1 (.out_3(out_1), .in_2(8'ha6), .in_1(clock_1_out));
  Clock clock_1 (.out(clock_1_out));
endmodule

module ALU (
  input  [7:0] in_1,
  input  [7:0] in_2,
  input  in_3,
  output [7:0] out_4
);

  wire [7:0] adder_1_out, multiplexer_1_out, not_1_out;

  assign not_1_out = ~in_2;  // NOT_Gate not_1, 8 bits wide
  Adder adder_1 (.a(not_1_out), .b(8'h1), .out(adder_1_out));  // open: cin, cout
  Multiplexer #(.width(8)) multiplexer_1 (
    .in0(adder_1_out), .in1(in_2), .out(multiplexer_1_out), .sel(in_3));  // open: en
  Adder adder_2 (.a(in_1), .b(multiplexer_1_out), .out(out_4));  // open: cin, cout
endmodule

module LU (
  input  [7:0] in_1,
  input  [7:0] in_2,
  input  in_3,
  output [7:0] out_4
);

  wire [7:0] and_1_out, or_1_out;

  assign and_1_out = in_1 & in_2;  // AND_Gate and_1, 8 bits wide
  assign or_1_out = in_1 | in_2;  // OR_Gate or_1, 8 bits wide
  Multiplexer #(.width(8)) multiplexer_1 (.in0(or_1_out), .in1(and_1_out), .out(out_4), .sel(in_3));  // open: en
endmodule

module ALU_T (
  input  [7:0] in_1,
  input  [7:0] in_2,
  input  [3:0] in_3,
  output [7:0] out_4
);

  wire [7:0] alu_1_out_4, lu_1_out_4;

  LU lu_1 (.out_4(lu_1_out_4), .in_1(in_1), .in_2(in_2), .in_3(in_3[0]));
  ALU alu_1 (.in_1(in_1), .in_2(in_2), .in_3(in_3[1]), .out_4(alu_1_out_4));
  Multiplexer #(.width(8)) multiplexer_1 (.in0(lu_1_out_4), .in1(alu_1_out_4), .out(out_4), .sel(in_3[2]));  // open: en
endmodule

module \寄存器组  (
  input  [7:0] in_1,
  input  [4:0] in_2,
  input  in_3,
  input  in_4,
  input  [4:0] in_5,
  output [7:0] out_6
);

  wire and_1_out, and_2_out, and_3_out, and_4_out, and_5_out, and_6_out, and_7_out, and_8_out,
       decoder_1_out0, decoder_1_out1, decoder_1_out2, decoder_1_out3, decoder_1_out4, decoder_1_out5,
       decoder_1_out6, decoder_1_out7;
  wire [7:0] main_1_out_3, main_2_out_3, main_3_out_3, main_4_out_3, main_5_out_3, main_6_out_3,
       main_7_out_3, main_8_out_3, multiplexer_1_out;

  Decoder #(.select(3)) decoder_1 (
    .out0(decoder_1_out0), .out1(decoder_1_out1), .out2(decoder_1_out2), .out3(decoder_1_out3),
    .out4(decoder_1_out4), .out5(decoder_1_out5), .out6(decoder_1_out6), .out7(decoder_1_out7),
    .sel(in_2[2:0]));  // open: en
  and and_1 (and_1_out, in_4, decoder_1_out0);
  and and_2 (and_2_out, in_4, decoder_1_out1);
  and and_3 (and_3_out, in_4, decoder_1_out2);
  and and_4 (and_4_out, decoder_1_out3, in_4);
  and and_5 (and_5_out, in_4, decoder_1_out4);
  and and_6 (and_6_out, in_4, decoder_1_out5);
  and and_7 (and_7_out, decoder_1_out6, in_4);
  and and_8 (and_8_out, decoder_1_out7, in_4);
  main main_1 (.out_3(main_1_out_3), .in_2(in_1), .in_1(and_1_out));
  main main_2 (.out_3(main_2_out_3), .in_2(in_1), .in_1(and_2_out));
  main main_3 (.out_3(main_3_out_3), .in_2(in_1), .in_1(and_3_out));
  main main_4 (.out_3(main_4_out_3), .in_2(in_1), .in_1(and_4_out));
  main main_5 (.out_3(main_5_out_3), .in_2(in_1), .in_1(and_5_out));
  main main_6 (.out_3(main_6_out_3), .in_2(in_1), .in_1(and_6_out));
  main main_7 (.out_3(main_7_out_3), .in_2(in_1), .in_1(and_7_out));
  main main_8 (.out_3(main_8_out_3), .in_2(in_1), .in_1(and_8_out));
  Multiplexer #(.select(3), .width(8)) multiplexer_1 (
    .in0(main_1_out_3), .in1(main_2_out_3), .in2(main_3_out_3), .in3(main_4_out_3), .in4(main_5_out_3),
    .in5(main_6_out_3), .in6(main_7_out_3), .in7(main_8_out_3), .out(multiplexer_1_out), .sel(in_5[2:0]),
    .en(in_3));
  Multiplexer #(.width(8)) multiplexer_2 (
    .in0({8{1'b0}}), .in1(multiplexer_1_out), .out(out_6), .sel(in_3));  // open: en
endmodule

module CPU (
);

  wire clock_1_out, clock_2_out, not_1_out;
  wire [3:0] bit_extender_1_out;
  wire [7:0] alu_t_1_out_4, bit_extender_2_out, multiplexer_1_out, ram_1_data, \寄存器组_1_out_6 ;

  Bit_Extender #(.in_width(6), .out_width(4)) bit_extender_1 (.in(6'b000110), .out(bit_extender_1_out));
  Bit_Extender #(.in_width(10), .out_width(8)) bit_extender_2 (.in(10'h1), .out(bit_extender_2_out));
  \寄存器组  \u_寄存器组_1  (
    .in_1(multiplexer_1_out), .in_4(1'b1), .in_5({5{1'b0}}), .out_6(\寄存器组_1_out_6 ), .in_2(5'b00001),
    .in_3(clock_1_out));
  Clock clock_1 (.out(clock_1_out));
  ALU_T alu_t_1 (.in_1(\寄存器组_1_out_6 ), .in_2(bit_extender_2_out), .in_3(bit_extender_1_out), .out_4(alu_t_1_out_4));
  Multiplexer #(.width(8)) multiplexer_1 (
    .in0(alu_t_1_out_4), .in1(ram_1_data), .out(multiplexer_1_out), .sel(1'b0));  // open: en
  not not_1 (not_1_out, 1'b0);
  Clock clock_2 (.out(clock_2_out));
  RAM #(.bus("separate")) ram_1 (
    .addr(8'h1), .din(\寄存器组_1_out_6 ), .data(ram_1_data), .str(1'b0), .clk(clock_2_out), .ld(not_1_out));  // open: sel, clr
endmodule
