// Logisim project DQ锁存器.circ as structural Verilog: 1 circuit, main circuit main
module main (
  output out_1,
  output out_2,
  output out_3
);

  wire clock_1_out, nand_1_out, nand_2_out, not_1_out, not_2_out;

  Clock clock_1 (.out(clock_1_out));
  not not_1 (not_1_out, 1'b0);
  not not_2 (not_2_out, clock_1_out);
  nand nand_1 (nand_1_out, 1'b0, 1'b0);
  nand nand_2 (nand_2_out, 1'b0, not_1_out);
  and and_1 (out_1, not_2_out, clock_1_out);
  nand nand_3 (out_2, nand_1_out, out_3, out_3);
  nand nand_4 (out_3, out_2, nand_2_out);
endmodule
