// Logisim project 全加器.circ as structural Verilog: 1 circuit, main circuit main
module main (
  output out_1,
  output out_2,
  output out_3
);

  wire and_1_out, and_2_out, and_3_out, and_4_out, or_1_out, xor_1_out, xor_2_out;

  xor xor_1 (xor_1_out, 1'b0, 1'b0);
  ExactlyOne xor_2 (.out(xor_2_out), .in0(1'b1), .in1(1'b1), .in3(1'b1));
  and and_1 (and_1_out, 1'b0, 1'b0);
  and and_2 (and_2_out, xor_1_out, 1'b1);
  and and_3 (and_3_out, 1'b1, 1'b1);
  and and_4 (and_4_out, or_1_out, xor_2_out);
  ExactlyOne xor_3 (.out(out_1), .in0(xor_1_out), .in1(xor_1_out), .in2(1'b1));
  or or_1 (or_1_out, and_1_out, and_2_out, and_2_out);
  ExactlyOne xor_4 (.out(out_2), .in0(xor_2_out), .in1(xor_2_out), .in3(or_1_out));
  or or_2 (out_3, and_3_out, and_3_out, and_4_out, and_4_out, and_4_out);
endmodule
